// Logisim project cpu.circ as structural Verilog: 7 circuits, main circuit main
module main (
  input  reset
);

  wire ALUsrc, clk, controller_npc_sel, ExtOp, IfBeqZero, mem2reg, memread, memwrite, not_1_out, regdst,
       register_2_q, regwrite, zero;
  wire [1:0] ALUOp;
  wire [3:0] ALUControl_aluoperate;
  wire [4:0] multiplexer_4_out, register_1_q, wreg;
  wire [15:0] ext;
  wire [31:0] A, B, PCBeq, ram_1_data, re, wd, wdata;
  wire [31:16] instr;

  // Probe on {instr, ext}
  // Probe on instr[31:26]
  // Probe on ext
  // Probe on ext[5:0]
  Clock u_clk (.out(clk));
  IFU IFU (.IfBeqZero(IfBeqZero), .instr({instr, ext}), .PCBeq(PCBeq), .clk(clk), .reset(reset));
  // Probe on instr[25:21]
  // Probe on instr[20:16]
  // Probe on wreg
  // Probe on ext[5:0]
  // Probe on wdata
  // Probe on A
  // Probe on B
  Multiplexer #(.width(5)) multiplexer_1 (.in0(instr[20:16]), .in1(ext[15:11]), .out(wreg), .sel(regdst), .en(clk));
  Control controller (
    .opcode(instr[31:26]), .regdst(regdst), .alusrc(ALUsrc), .mem2reg(mem2reg), .regwrite(regwrite),
    .memwrite(memwrite), .nPC_Sel(controller_npc_sel), .ExtOp(ExtOp), .ALUOp(ALUOp), .memread(memread),
    .clk(clk), .clk1(clk));
  RegFile \reg  (
    .reg1(instr[25:21]), .wreg(wreg), .regwrite(regwrite), .wdata(wdata), .reg2(instr[20:16]), .Rdata1(A),
    .Rdata2(wd), .clk(clk));
  // Probe on re
  Extender extender (.in_1(ext), .ExtOp(ExtOp), .out_4(PCBeq), .clk(clk));
  // Probe on ALUOp
  // Probe on wd
  Multiplexer #(.width(32)) multiplexer_2 (.in0(wd), .in1(PCBeq), .out(B), .sel(ALUsrc));  // open: en
  ALU alu (.A(A), .B(B), .result(re), .Zero(zero), .ALUOperate(ALUControl_aluoperate));
  ALUControl ALUControl (.Funct(ext[5:0]), .in_2(ALUOp), .ALUOperate(ALUControl_aluoperate));
  and and_1 (IfBeqZero, zero, controller_npc_sel);
  // Probe on ALUControl_aluoperate
  Multiplexer #(.width(32)) multiplexer_3 (.in0(re), .in1(ram_1_data), .out(wdata), .sel(mem2reg));  // open: en
  Register #(.width(5), .trigger("falling")) register_1 (.D(re[4:0]), .Q(register_1_q), .clk(clk));  // open: en, clr
  Multiplexer #(.width(5)) multiplexer_4 (.in0(re[4:0]), .out(multiplexer_4_out), .sel(memwrite));  // open: in1, en
  RAM #(.addrWidth(5), .dataWidth(32), .bus("separate")) ram_1 (
    .addr(re[4:0]), .din(wd), .data(ram_1_data), .str(memwrite), .sel(1'b1), .clk(not_1_out), .ld(memread));  // open: clr
  Register #(.width(1), .trigger("falling")) register_2 (.D(memwrite), .Q(register_2_q), .clk(clk));  // open: en, clr
  not not_1 (not_1_out, clk);

  // Other names for the same wires on the sheet: funct[5:0] = ext[5:0]; instr[15:0] = ext; opcode[5:0] = instr[31:26];
  //   reg[4:0] = instr[25:21]; reg2[4:0] = instr[20:16]

  // Notes on the sheet:
  //   IFU OutPut Test:
  //   Reg Input Test
  //   ALU Test
  //   opcode
  //   funct
  //   ExtOp
  //   DM test
  //   regdst
  //   ALUsrc
  //   mem2reg
  //   regwrite
  //   memwrite
  //   nPC_Sef
  //   ALUOp
endmodule

module RegFile (
  input  [4:0] reg1,
  input  [4:0] wreg,
  input  clk,
  input  regwrite,
  input  [31:0] wdata,
  input  [4:0] reg2,
  output [31:0] Rdata1,
  output [31:0] Rdata2
);

  wire and_1_out, and_2_out, and_3_out, and_4_out, and_5_out, and_6_out, and_7_out, and_8_out, and_9_out,
       and_10_out, and_11_out, and_12_out, and_13_out, and_14_out, and_15_out, and_16_out, and_17_out,
       and_18_out, and_19_out, and_20_out, and_21_out, and_22_out, and_23_out, and_24_out, and_25_out,
       and_26_out, and_27_out, and_28_out, and_29_out, and_30_out, and_31_out, and_32_out, decoder_1_out0,
       decoder_1_out1, decoder_1_out2, decoder_1_out3, decoder_1_out4, decoder_1_out5, decoder_1_out6,
       decoder_1_out7, decoder_1_out8, decoder_1_out9, decoder_1_out10, decoder_1_out11, decoder_1_out12,
       decoder_1_out13, decoder_1_out14, decoder_1_out15, decoder_1_out16, decoder_1_out17, decoder_1_out18,
       decoder_1_out19, decoder_1_out20, decoder_1_out21, decoder_1_out22, decoder_1_out23, decoder_1_out24,
       decoder_1_out25, decoder_1_out26, decoder_1_out27, decoder_1_out28, decoder_1_out29, decoder_1_out30,
       decoder_1_out31;
  wire [31:0] reg0_q, reg1_q, reg2_q, reg3_q, reg4_q, reg5_q, reg6_q, reg7_q, reg8_q, reg9_q, reg10_q,
       reg11_q, reg12_q, reg13_q, reg14_q, reg15_q, reg16_q, reg17_q, reg18_q, reg19_q, reg20_q, reg21_q,
       reg22_q, reg23_q, reg24_q, reg25_q, reg26_q, reg27_q, reg28_q, reg29_q, reg30_q, reg31_q;

  Clock clock_1 ();  // open: out
  // Probe on wdata
  Decoder #(.select(5), .enable("false")) decoder_1 (
    .out0(decoder_1_out0), .out1(decoder_1_out1), .out2(decoder_1_out2), .out3(decoder_1_out3),
    .out4(decoder_1_out4), .out5(decoder_1_out5), .out6(decoder_1_out6), .out7(decoder_1_out7),
    .out8(decoder_1_out8), .out9(decoder_1_out9), .out10(decoder_1_out10), .out11(decoder_1_out11),
    .out12(decoder_1_out12), .out13(decoder_1_out13), .out14(decoder_1_out14), .out15(decoder_1_out15),
    .out16(decoder_1_out16), .out17(decoder_1_out17), .out18(decoder_1_out18), .out19(decoder_1_out19),
    .out20(decoder_1_out20), .out21(decoder_1_out21), .out22(decoder_1_out22), .out23(decoder_1_out23),
    .out24(decoder_1_out24), .out25(decoder_1_out25), .out26(decoder_1_out26), .out27(decoder_1_out27),
    .out28(decoder_1_out28), .out29(decoder_1_out29), .out30(decoder_1_out30), .out31(decoder_1_out31),
    .sel(wreg));
  and and_1 (and_1_out, decoder_1_out1, 1'b1, regwrite);
  and and_2 (and_2_out, decoder_1_out2, 1'b1, regwrite);
  and and_3 (and_3_out, decoder_1_out3, 1'b1, regwrite);
  and and_4 (and_4_out, decoder_1_out4, 1'b1, regwrite);
  and and_5 (and_5_out, decoder_1_out5, 1'b1, regwrite);
  and and_6 (and_6_out, decoder_1_out6, 1'b1, regwrite);
  and and_7 (and_7_out, decoder_1_out7, 1'b1, regwrite);
  and and_8 (and_8_out, decoder_1_out8, 1'b1, regwrite);
  and and_9 (and_9_out, decoder_1_out9, 1'b1, regwrite);
  and and_10 (and_10_out, decoder_1_out10, 1'b1, regwrite);
  and and_11 (and_11_out, decoder_1_out11, 1'b1, regwrite);
  and and_12 (and_12_out, decoder_1_out12, 1'b1, regwrite);
  and and_13 (and_13_out, decoder_1_out13, 1'b1, regwrite);
  and and_14 (and_14_out, decoder_1_out14, 1'b1, regwrite);
  and and_15 (and_15_out, decoder_1_out15, 1'b1, regwrite);
  and and_16 (and_16_out, decoder_1_out16, 1'b1, regwrite);
  and and_17 (and_17_out, decoder_1_out17, 1'b1, regwrite);
  and and_18 (and_18_out, decoder_1_out18, 1'b1, regwrite);
  and and_19 (and_19_out, decoder_1_out19, 1'b1, regwrite);
  and and_20 (and_20_out, decoder_1_out20, 1'b1, regwrite);
  and and_21 (and_21_out, decoder_1_out21, 1'b1, regwrite);
  and and_22 (and_22_out, decoder_1_out22, 1'b1, regwrite);
  and and_23 (and_23_out, decoder_1_out23, 1'b1, regwrite);
  and and_24 (and_24_out, decoder_1_out24, 1'b1, regwrite);
  and and_25 (and_25_out, decoder_1_out25, 1'b1, regwrite);
  and and_26 (and_26_out, decoder_1_out26, 1'b1, regwrite);
  and and_27 (and_27_out, decoder_1_out27, 1'b1, regwrite);
  and and_28 (and_28_out, decoder_1_out28, 1'b1, regwrite);
  and and_29 (and_29_out, decoder_1_out29, 1'b1, regwrite);
  and and_30 (and_30_out, decoder_1_out30, 1'b1, regwrite);
  and and_31 (and_31_out, decoder_1_out31, 1'b1, regwrite);
  and and_32 (and_32_out, decoder_1_out0, 1'b1, regwrite);
  Register #(.width(32), .trigger("falling")) reg0 (.D(wdata), .en(and_32_out), .Q(reg0_q), .clk(clk), .clr(1'b1));
  Register #(.width(32), .trigger("falling")) u_reg2 (.D(wdata), .en(and_2_out), .Q(reg2_q), .clk(clk));  // open: clr
  Register #(.width(32), .trigger("falling")) reg4 (.D(wdata), .en(and_4_out), .Q(reg4_q), .clk(clk));  // open: clr
  Register #(.width(32), .trigger("falling")) reg6 (.D(wdata), .en(and_6_out), .Q(reg6_q), .clk(clk));  // open: clr
  Register #(.width(32), .trigger("falling")) reg8 (.D(wdata), .en(and_8_out), .Q(reg8_q), .clk(clk));  // open: clr
  Register #(.width(32), .trigger("falling")) reg10 (.D(wdata), .en(and_10_out), .Q(reg10_q), .clk(clk));  // open: clr
  Register #(.width(32), .trigger("falling")) reg12 (.D(wdata), .en(and_12_out), .Q(reg12_q), .clk(clk));  // open: clr
  Register #(.width(32), .trigger("falling")) reg14 (.D(wdata), .en(and_14_out), .Q(reg14_q), .clk(clk));  // open: clr
  Register #(.width(32), .trigger("falling")) reg16 (.D(wdata), .en(and_16_out), .Q(reg16_q), .clk(clk));  // open: clr
  Register #(.width(32), .trigger("falling")) reg18 (.D(wdata), .en(and_18_out), .Q(reg18_q), .clk(clk));  // open: clr
  Register #(.width(32), .trigger("falling")) reg20 (.D(wdata), .en(and_20_out), .Q(reg20_q), .clk(clk));  // open: clr
  Register #(.width(32), .trigger("falling")) reg22 (.D(wdata), .en(and_22_out), .Q(reg22_q), .clk(clk));  // open: clr
  Register #(.width(32), .trigger("falling")) reg24 (.D(wdata), .en(and_24_out), .Q(reg24_q), .clk(clk));  // open: clr
  Register #(.width(32), .trigger("falling")) reg26 (.D(wdata), .en(and_26_out), .Q(reg26_q), .clk(clk));  // open: clr
  Register #(.width(32), .trigger("falling")) reg28 (.D(wdata), .en(and_28_out), .Q(reg28_q), .clk(clk));  // open: clr
  Register #(.width(32), .trigger("falling")) reg30 (.D(wdata), .en(and_30_out), .Q(reg30_q), .clk(clk));  // open: clr
  Register #(.width(32), .trigger("falling")) u_reg1 (.D(wdata), .en(and_1_out), .Q(reg1_q), .clk(clk));  // open: clr
  Register #(.width(32), .trigger("falling")) reg3 (.D(wdata), .en(and_3_out), .Q(reg3_q), .clk(clk));  // open: clr
  Register #(.width(32), .trigger("falling")) reg5 (.D(wdata), .en(and_5_out), .Q(reg5_q), .clk(clk));  // open: clr
  Register #(.width(32), .trigger("falling")) reg7 (.D(wdata), .en(and_7_out), .Q(reg7_q), .clk(clk));  // open: clr
  Register #(.width(32), .trigger("falling")) reg9 (.D(wdata), .en(and_9_out), .Q(reg9_q), .clk(clk));  // open: clr
  Register #(.width(32), .trigger("falling")) reg11 (.D(wdata), .en(and_11_out), .Q(reg11_q), .clk(clk));  // open: clr
  Register #(.width(32), .trigger("falling")) reg13 (.D(wdata), .en(and_13_out), .Q(reg13_q), .clk(clk));  // open: clr
  Register #(.width(32), .trigger("falling")) reg15 (.D(wdata), .en(and_15_out), .Q(reg15_q), .clk(clk));  // open: clr
  Register #(.width(32), .trigger("falling")) reg17 (.D(wdata), .en(and_17_out), .Q(reg17_q), .clk(clk));  // open: clr
  Register #(.width(32), .trigger("falling")) reg19 (.D(wdata), .en(and_19_out), .Q(reg19_q), .clk(clk));  // open: clr
  Register #(.width(32), .trigger("falling")) reg21 (.D(wdata), .en(and_21_out), .Q(reg21_q), .clk(clk));  // open: clr
  Register #(.width(32), .trigger("falling")) reg23 (.D(wdata), .en(and_23_out), .Q(reg23_q), .clk(clk));  // open: clr
  Register #(.width(32), .trigger("falling")) reg25 (.D(wdata), .en(and_25_out), .Q(reg25_q), .clk(clk));  // open: clr
  Register #(.width(32), .trigger("falling")) reg27 (.D(wdata), .en(and_27_out), .Q(reg27_q), .clk(clk));  // open: clr
  Register #(.width(32), .trigger("falling")) reg29 (.D(wdata), .en(and_29_out), .Q(reg29_q), .clk(clk));  // open: clr
  Register #(.width(32), .trigger("falling")) reg31 (.D(wdata), .en(and_31_out), .Q(reg31_q), .clk(clk));  // open: clr
  Multiplexer #(.select(5), .width(32)) multiplexer_1 (
    .in0(reg0_q), .in1(reg1_q), .in2(reg2_q), .in3(reg3_q), .in4(reg4_q), .in5(reg5_q), .in6(reg6_q),
    .in7(reg7_q), .in8(reg8_q), .in9(reg9_q), .in10(reg10_q), .in11(reg11_q), .in12(reg12_q), .in13(reg13_q),
    .in14(reg14_q), .in15(reg15_q), .in16(reg16_q), .in17(reg17_q), .in18(reg18_q), .in19(reg19_q),
    .in20(reg20_q), .in21(reg21_q), .in22(reg22_q), .in23(reg23_q), .in24(reg24_q), .in25(reg25_q),
    .in26(reg26_q), .in27(reg27_q), .in28(reg28_q), .in29(reg29_q), .in30(reg30_q), .in31(reg31_q),
    .out(Rdata1), .sel(reg1));  // open: en
  Multiplexer #(.select(5), .width(32)) multiplexer_2 (
    .in0(reg0_q), .in1(reg1_q), .in2(reg2_q), .in3(reg3_q), .in4(reg4_q), .in5(reg5_q), .in6(reg6_q),
    .in7(reg7_q), .in8(reg8_q), .in9(reg9_q), .in10(reg10_q), .in11(reg11_q), .in12(reg12_q), .in13(reg13_q),
    .in14(reg14_q), .in15(reg15_q), .in16(reg16_q), .in17(reg17_q), .in18(reg18_q), .in19(reg19_q),
    .in20(reg20_q), .in21(reg21_q), .in22(reg22_q), .in23(reg23_q), .in24(reg24_q), .in25(reg25_q),
    .in26(reg26_q), .in27(reg27_q), .in28(reg28_q), .in29(reg29_q), .in30(reg30_q), .in31(reg31_q),
    .out(Rdata2), .sel(reg2));  // open: en
  // Probe on reg1

  // Notes on the sheet:
  //   reg2: pull=up
  //   reg1: pull=up
endmodule

module ALU (
  input  [31:0] A,
  input  [31:0] B,
  input  [3:0] ALUOperate,
  output [31:0] result,
  output Zero
);

  wire clock_1_out, comparator_1_eq, decoder_1_out0, decoder_1_out1, decoder_1_out2, decoder_1_out6;
  wire [1:0] priority_encoder_1_out;
  wire [31:0] adder_1_out, multiplexer_1_out, multiplexer_2_out, or_1_out, shifter_1_out, subtractor_1_out;

  Clock clock_1 (.out(clock_1_out));
  Multiplexer #(.width(32)) multiplexer_1 (
    .in0({32{1'b0}}), .in1(B), .out(multiplexer_1_out), .sel(clock_1_out));  // open: en
  Decoder #(.select(4)) decoder_1 (
    .out0(decoder_1_out0), .out1(decoder_1_out1), .out2(decoder_1_out2), .out6(decoder_1_out6),
    .sel(ALUOperate));  // open: out3, out4, out5, out7, out8, out9, out10, out11, out12, out13, out14, out15, en
  Multiplexer #(.width(32)) multiplexer_2 (
    .in0({32{1'b0}}), .in1(A), .out(multiplexer_2_out), .sel(clock_1_out));  // open: en
  Shifter #(.width(32)) shifter_1 (.in(multiplexer_1_out), .\dist (5'b10000), .out(shifter_1_out));
  assign or_1_out = multiplexer_2_out | multiplexer_1_out;  // OR_Gate or_1, 32 bits wide
  Priority_Encoder #(.select(2)) priority_encoder_1 (
    .in0(decoder_1_out0), .in1(decoder_1_out1), .in2(decoder_1_out2), .in3(decoder_1_out6),
    .out(priority_encoder_1_out));  // open: gs, en_out, en_in
  Adder #(.width(32)) adder_1 (.a(multiplexer_2_out), .b(multiplexer_1_out), .out(adder_1_out));  // open: cin, cout
  Subtractor #(.width(32)) subtractor_1 (
    .a(multiplexer_2_out), .b(multiplexer_1_out), .out(subtractor_1_out));  // open: bin, bout
  Comparator #(.width(32)) comparator_1 (.a(subtractor_1_out), .b({32{1'b0}}), .eq(comparator_1_eq));  // open: gt, lt
  // Probe on shifter_1_out
  // Probe on priority_encoder_1_out
  Multiplexer #(.select(2), .width(32)) multiplexer_3 (
    .in0(shifter_1_out), .in1(or_1_out), .in2(adder_1_out), .in3(subtractor_1_out), .out(result),
    .sel(priority_encoder_1_out), .en(clock_1_out));
  Multiplexer multiplexer_4 (.in0(1'b0), .in1(comparator_1_eq), .out(Zero), .sel(clock_1_out));  // open: en
endmodule

module Control (
  input  [5:0] opcode,
  input  clk1,
  input  clk,
  output regdst,
  output alusrc,
  output mem2reg,
  output regwrite,
  output memwrite,
  output memread,
  output nPC_Sel,
  output ExtOp,
  output [1:0] ALUOp
);

  wire clock_1_out, lui_out, not_1_out, not_2_out, not_3_out, not_4_out, not_5_out, not_6_out, not_7_out,
       not_8_out, not_9_out, not_10_out, not_11_out, not_12_out, not_13_out, not_14_out, not_15_out,
       not_16_out, not_17_out, not_18_out, not_19_out, not_20_out, not_21_out, ori_out;

  not not_1 (not_1_out, opcode[2]);
  not not_2 (not_2_out, opcode[5]);
  not not_3 (not_3_out, opcode[3]);
  not not_4 (not_4_out, opcode[4]);
  and R_Format (regdst, not_2_out, not_4_out, not_3_out, clk, not_1_out, not_7_out, not_6_out);
  Clock clock_1 (.out(clock_1_out));
  not not_5 (not_5_out, opcode[4]);
  not not_6 (not_6_out, opcode[0]);
  not not_7 (not_7_out, opcode[1]);
  not not_8 (not_8_out, opcode[3]);
  not not_9 (not_9_out, opcode[2]);
  and LW (mem2reg, opcode[5], not_5_out, not_8_out, clk, not_9_out, opcode[1], opcode[0]);
  not not_10 (not_10_out, opcode[4]);
  not not_11 (not_11_out, opcode[2]);
  and SW (memwrite, opcode[5], not_10_out, opcode[3], clk, not_11_out, opcode[1], opcode[0]);
  not not_12 (not_12_out, opcode[3]);
  not not_13 (not_13_out, opcode[5]);
  not not_14 (not_14_out, opcode[4]);
  and Beq (nPC_Sel, not_13_out, not_14_out, not_12_out, clk, opcode[2], not_18_out, not_15_out);
  not not_15 (not_15_out, opcode[0]);
  not not_16 (not_16_out, opcode[4]);
  not not_17 (not_17_out, opcode[5]);
  not not_18 (not_18_out, opcode[1]);
  not not_19 (not_19_out, opcode[1]);
  not not_20 (not_20_out, opcode[5]);
  and ori (ori_out, not_17_out, not_16_out, opcode[3], clk, opcode[2], not_19_out, opcode[0]);
  not not_21 (not_21_out, opcode[4]);
  and lui (lui_out, not_20_out, not_21_out, opcode[3], clk, opcode[2], opcode[1], opcode[0]);
  or or_1 (alusrc, lui_out, mem2reg, memwrite, ori_out);
  or or_2 (regwrite, lui_out, regdst, mem2reg, ori_out);
  or or_3 (ExtOp, mem2reg, memwrite, lui_out, ori_out, nPC_Sel);
  or or_4 (ALUOp[1], ori_out, lui_out, regdst);
  or or_5 (ALUOp[0], lui_out, nPC_Sel);

  assign memread = mem2reg;
endmodule

module IFU (
  input  IfBeqZero,
  input  [31:0] PCBeq,
  input  clk,
  input  reset,
  output [31:0] instr
);

  wire \PC复位_q ;
  wire [29:0] adder_1_out, adder_2_out, bit_extender_1_out, multiplexer_1_out, PC, PC_q;
  wire [31:0] shifter_1_out;

  J_K_Flip_Flop \PC复位  (.J(1'b0), .K(1'b0), .Q(\PC复位_q ), .preset(clk), .en(clk), .reset(reset));  // open: clk, Qn
  Multiplexer #(.width(30)) multiplexer_1 (
    .in0(30'h3000), .in1(PC), .out(multiplexer_1_out), .sel(\PC复位_q ));  // open: en
  Register #(.width(30)) u_PC (.D(multiplexer_1_out), .Q(PC_q), .clk(clk));  // open: en, clr
  Shifter #(.width(32)) shifter_1 (.in(PCBeq), .\dist (5'b00010), .out(shifter_1_out));
  // Probe on PC_q[4:0]
  Bit_Extender #(.in_width(32), .out_width(30)) bit_extender_1 (.in(shifter_1_out), .out(bit_extender_1_out));
  Adder #(.width(30)) adder_1 (.a(30'h1), .b(PC_q), .out(adder_1_out));  // open: cin, cout
  ROM #(.addrWidth(5), .dataWidth(32)) rom_1 (.addr(PC_q[4:0]), .data(instr), .sel(1'b1));
  Adder #(.width(30)) adder_2 (.a(bit_extender_1_out), .b(adder_1_out), .out(adder_2_out));  // open: cin, cout
  Multiplexer #(.width(30)) multiplexer_2 (
    .in0(adder_1_out), .in1(adder_2_out), .out(PC), .sel(IfBeqZero));  // open: en

  // Notes on the sheet:
  //   contents of rom_1 (hex, n*v repeats v):
  //   8c010001 8c020002 3c03007f 34250007 ac050003 ac050004 ac050005 ac050006 ac050007 ac050008 460021
endmodule

module Extender (
  input  [15:0] in_1,
  input  ExtOp,
  input  clk,
  output [31:0] out_4
);

  wire [15:0] multiplexer_1_out;

  assign out_4 = {{16{1'b0}}, multiplexer_1_out};  // Bit_Extender bit_extender_1
  Multiplexer #(.width(16)) multiplexer_1 (
    .in0({16{1'b0}}), .in1(in_1), .out(multiplexer_1_out), .sel(ExtOp), .en(clk));
endmodule

module ALUControl (
  input  [5:0] Funct,
  input  [1:0] in_2,
  output [3:0] ALUOperate
);

  wire decoder_1_out0, decoder_1_out1, decoder_1_out2, decoder_1_out3, decoder_2_out1, decoder_2_out3,
       decoder_2_out6, decoder_2_out7, or_1_out, or_2_out;

  // Probe on Funct[2:0]
  Decoder #(.select(2), .enable("false")) decoder_1 (
    .out0(decoder_1_out0), .out1(decoder_1_out1), .out2(decoder_1_out2), .out3(decoder_1_out3), .sel(in_2));
  Decoder #(.select(3)) decoder_2 (
    .out1(decoder_2_out1), .out3(decoder_2_out3), .out6(decoder_2_out6), .out7(decoder_2_out7),
    .sel(Funct[2:0]), .en(decoder_1_out2));  // open: out0, out2, out4, out5
  or or_1 (or_1_out, decoder_2_out1, decoder_1_out0);
  or or_2 (or_2_out, decoder_2_out3, decoder_1_out1);
  Priority_Encoder #(.select(4)) priority_encoder_1 (
    .in0(decoder_1_out3), .in1(decoder_2_out7), .in2(or_1_out), .in6(or_2_out), .out(ALUOperate));  // open: in3, in4, in5, in7, in8, in9, in10, in11, in12, in13, in14, in15, gs, en_out, en_in
  // Probe on ALUOperate
endmodule
